# Fritzing sketch schematic (saved by Fritzing 1.0.4)
breadboards: 1

parts:
  A1 = Esp32-c3 super mini
  A2 = max485 cd4069 module
  Power_plug1 = USB-C plug  # not connected
  XLR1 = XLR3_NCFAH2 [package=xlr3_nc3fah2]

nets:
  N1: A1.Pin_8, A2.Pin_2
  N2: A1.Pin_15, A2.Pin_4
  N3: A1.Pin_16, A2.Pin_1
  N4: A2.Pin_5, XLR1.1
  N5: A2.Pin_6, XLR1.G
  N6: A2.Pin_7, XLR1.3

notes:
  usb c power
  esp c3<module fritzingVersion="1.0.4.2024-10-07.CD-2051-0-a8c6ef7c">
  <boundingRects>
  <boundingRect name="Schematic View" rect="0 0 0 0"/>
  <boundingRect name="Breadboard View" rect="-30.3494 3.92469 69.2547 33"/>
  <boundingRect name="PCB View" rect="0 0 0 0"/>
  </boundingRects>
  <instances>
  <instance modelIndex="85410523" moduleIdRef="NoteModuleID" path=":/resources/parts/core/note.fzp">
  <title>Note1</title>
  <text>&lt;!DOCTYPE HTML PUBLIC "-//W3C//DTD HTML 4.0//EN" "http://www.w3.org/TR/REC-html40/strict.dtd">
  &lt;html>&lt;head>&lt;meta name="qrichtext" content="1" />&lt;meta charset="utf-8" />&lt;style type="text/css">
  p, li { white-space: pre-wrap; }
  hr { height: 1px; border-width: 0; }
  li.unchecked::marker { content: "\2610"; }
  li.checked::marker { content: "\2612"; }
  &lt;/style>&lt;/head>&lt;body style=" font-family:'Droid Sans'; font-size:9pt; font-weight:400; font-style:normal;">
  &lt;p style=" margin-top:0px; margin-bottom:0px; margin-left:0px; margin-right:0px; -qt-block-indent:0; text-indent:0px;">usb c power&lt;/p>&lt;/body>&lt;/html></text>
  <views>
  <breadboardView layer="breadboardNote">
  <geometry height="33" width="69.2547" x="-30.3494" y="3.92469" z="6.5"/>
  </breadboardView>
  </views>
  </instance>
  </instances>
  </module>
  supermini
  3 pin xlr female plug
  MAX485 CD4069 RS-485 to TTL

custom parts:
  Esp32-c3 super mini: ESP32-C3 Development Board ESP32 SuperMini Development Board ESP32 Development Board WiFi Bluetooth.
  max485 cd4069 module: Module,3.3V-5.5V 485 to Serial UART Level Mutual Conversion Hardware Automatic Flow Control Module.
  USB-C plug: power plug
